# Fritzing sketch lift (saved by Fritzing 0.9.3b)
breadboards: 2

parts:
  S1 = Pushbutton [package="[THT]"]
  S2 = Pushbutton [package="[THT]"]
  S3 = Pushbutton [package="[THT]"]
  R1 = Resistor [tolerance=±5% resistance=10k package=THT]
  R2 = Resistor [tolerance=±5% resistance=10k package=THT]
  R3 = Resistor [tolerance=±5% resistance=10k package=THT]
  Part1 = Arduino Uno (Rev3)
  R4 = Resistor [tolerance=±5% resistance=220 package=THT]
  R5 = Resistor [tolerance=±5% resistance=220 package=THT]
  R6 = Resistor [tolerance=±5% resistance=220 package=THT]
  LED1 = smd LED [color="Red (633nm)" package="1206 [SMD]"]
  LED2 = smd LED [color="Red (633nm)" package="1206 [SMD]"]
  LED3 = smd LED [color="Red (633nm)" package="1206 [SMD]"]
  L298N1 = L298N DC motor driver
  M1 = DC Motor  # not connected
  Part2 = Arduino Uno (Rev3) - ICSP
  Part3 = Bluetooth HC-05 Macho
  J2 = Infrared Proximity Sensor
  J3 = Infrared Proximity Sensor
  Part4 = LCD1602-I2C
  VCC1 = Battery block 9V  # not connected

nets:
  VCC: S1.Pin_1, S1.Pin_2, S2.Pin_1, S2.Pin_2, S3.Pin_1, S3.Pin_2, Part1.5V, L298N1.5V, Part3.VCC, J2.Vcc, J3.Vcc, Part4.VCC
  N1: S1.Pin_3, S1.Pin_4, R1.Pin_1, Part1.D2
  N2: S2.Pin_3, S2.Pin_4, R2.Pin_1, Part1.D3_PWM
  N3: S3.Pin_3, S3.Pin_4, R3.Pin_1, Part1.D4
  GND: R1.Pin_0, R2.Pin_0, R3.Pin_0, Part1.GND, LED1.anode, LED2.anode, LED3.anode, L298N1.GND, Part3.GND, J2.GND, J3.GND, Part4.GND
  N4: Part1.A4/SDA, Part4.SDA
  N5: Part1.A5/SCL, Part4.SCL
  N6: Part1.D12/MISO, R6.Pin_0
  N7: Part1.D13/SCK, R5.Pin_0
  N8: Part1.D5_PWM, J3.Vout
  N9: Part1.D6_PWM, J2.Vout
  N10: R4.Pin_1, LED1.cathode
  N11: R5.Pin_1, LED3.cathode
  N12: R6.Pin_1, LED2.cathode
  N13: L298N1.IN1, Part2.D9_PWM
  N14: L298N1.IN2, Part2.D10_PWM/SS
  N15: Part2.D8, Part3.TXD
  N16: Part2.D7, Part3.RXD

custom parts:
  L298N DC motor driver: 2x DC motor driver with 78M05 positive voltage regulator (7..35 V) L298N: max 46 V, 2 A Set 5 V Enable jumper to enable 5 V regultor (needed for the L298N) and +5 V output at screw terminal or supply external +5 V at screw terminal Set ENA and/or ENB to +5 V to enable motor permanently or supply ENA and/or ENB with PWM signal IN1 and IN2 set rotation directory for motor A (OUT1/OUT2) IN2 and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
  LCD1602-I2C: A standard character display, usually with 2x16 characters. Comes in many colors with LCM1602 IIC attached.
